# Fritzing sketch PiGMI (saved by Fritzing 0.9.1b)
circuit board: 8.46667cm x 5.64444cm
breadboards: 1

parts:
  Raspberry_Pi1 = Raspberry Pi B+
  S1 = Reed switch [package=THT]
  U1 = G3VM-61E1 [package=g3vm-61e1]
  U2 = G3VM-61E1 [package=g3vm-61e1]
  U3 = G3VM-61E1 [package=g3vm-61e1]
  S2 = Reed switch [package=THT]
  S3 = Reed switch [package=THT]
  S4 = SWITCH-MOMENTARY-2 [package=tactile_switch_tall]
  S5 = SWITCH-MOMENTARY-2 [package=tactile_switch_tall]
  S6 = SWITCH-MOMENTARY-2 [package=tactile_switch_tall]

nets:
  3V3: Raspberry_Pi1.3v3, Raspberry_Pi1.3V3, U1.P$3, U2.P$3, U3.P$3
  N1: Raspberry_Pi1.GND, S1.pin_1, U1.P$1, U2.P$1, U3.P$1, S2.pin_1, S3.pin_1
  N2: Raspberry_Pi1.GPIO17, U2.P$2
  N3: Raspberry_Pi1.GPIO22, U3.P$2
  N4: Raspberry_Pi1.GPIO25, S2.pin_2
  N5: Raspberry_Pi1.GPIO24, Raspberry_Pi1.GPIO23, S1.pin_2, S3.pin_2
  N6: Raspberry_Pi1.GPIO18, U1.P$2
  N7: U1.P$5, S4.1
  N8: U1.P$6, S4.2
  N9: U2.P$5, S5.1
  N10: U2.P$6, S5.2
  N11: U3.P$5, S6.1
  N12: U3.P$6, S6.2

notes:
  Relay power is tied(red); Relay ground is tied(black). Switch ground is tied(black). GPIO pins may be changed during project build. Must be mapped correctly to software.
  Relays are wired accross the push buttons. One per door
  Magnet switches. Magnets are attached to door and move. One per door.
